// Logisim project Exp0_Logisim使用说明.circ as structural Verilog: 6 circuits, main circuit 接线颜色说明
module \接线颜色说明  (
  output out_1
);

  wire not_1_out, undriven;

  not not_1 (not_1_out, undriven);
  // Pins of 1 and 2 bits meet at 2'b00

  assign out_1 = 1'b0;

  // Notes on the sheet:
  //   亮绿色-高电平(1)
  //   墨绿色-高电平(0)
  //   蓝色-状态未知(x)
  //   灰色-未连接(-)
  //   橙色-位宽错误
  //   黑色-多位宽(Binary/Signed Decimal)
  //   使用手型工具点击线缆，可以看到线缆上承载的值
  //   红色-信号冲突(E)
endmodule

module \基本线路和接口  (
  input  \_0_1输入 ,
  input  \_0_1_x输入 ,
  input  [7:0] in_3,
  input  in_4,
  output \三态输出 ,
  output \_0_1输出 ,
  output \三态输出_2 ,
  output \_0_1输出_2 ,
  output out_9,
  output out_10,
  output out_11,
  output out_12,
  output [7:0] out_13,
  output [1:0] out_14
);

  Clock \u_时钟信号  (.out(out_9));
  Clock #(.highDuration(2), .lowDuration(3)) \u_时钟信号_2  (.out(out_10));
  // Probe on 1'b1
  // Probe on {8{1'b1}}
  // Probe on 8'h94
  // Probe on 8'h94
  // Probe on 8'h94
  // Probe on 1'b0
  // Probe on {8{1'b0}}
  // Probe on 8'h94
  // Probe on 2'b00
  // Probe on 8'h94

  assign \_0_1输出  = \_0_1输入 ;
  assign \_0_1输出_2  = \_0_1_x输入 ;
  assign out_11 = 1'b0;
  assign out_12 = in_4;
  assign out_13 = {in_3[7:6], 1'b0, in_3[6], in_3[3], in_3[5], in_3[1:0]};
  assign out_14 = 2'b00;
  assign \三态输出  = \_0_1输入 ;
  assign \三态输出_2  = \_0_1_x输入 ;

  // Other names for the same wires on the sheet: Variable = in_4

  // Notes on the sheet:
  //   常数
  //   输入Pin / 输出Pout / 时钟Clock
  //   分线器 Splitter
  //   时钟信号可以设置高/低电平持续时间
  //   分线器可以用作输入和输出
  //   每位值只能出现在最多一个端口
  //   探针 Probe
  //   隧道 Tunnel
  //   电源Power / 接地Ground
  //   探针无需设定位数
  //   同名隧道连接隧道两段的接线
  //   只有一个隧道为输入，其余为输出
  //   电源为全1
  //   接地为全0
endmodule

module \门电路  (
  input  [3:0] in_1,
  input  in_2,
  input  in_3,
  input  in_4,
  input  in_5,
  input  in_6,
  input  in_7,
  input  in_8,
  input  \_1为输入值_0为高阻态 ,
  input  in_10,
  output out_11,
  output out_12,
  output [3:0] out_13,
  output [3:0] out_14,
  output out_15,
  output out_16,
  output [3:0] out_17,
  output [3:0] out_18,
  output out_19,
  output out_20,
  output [3:0] out_21,
  output [3:0] out_22,
  output out_23,
  output [3:0] out_24,
  output [3:0] out_25,
  output [3:0] out_26
);

  wire and_3_out, and_4_out, buffer_1_out, button_1_out, not_3_out;

  assign out_25 = \_1为输入值_0为高阻态  ? in_1 : 4'bz;  // Controlled_Buffer controlled_buffer_1
  and and_1 (out_11, in_2, 1'b1);
  assign out_13 = in_1 & 4'b1011 & 4'b0011;  // AND_Gate and_2, 4 bits wide
  or or_1 (out_15, in_4, 1'b1);
  assign out_17 = in_1 | 4'b1001 | 4'b0001;  // OR_Gate or_2, 4 bits wide
  xor xor_1 (out_19, in_6, 1'b1);
  ExactlyOne xor_2[3:0] (.out(out_21), .in0(in_1), .in1(4'b1001), .in2(4'b0001));
  not not_1 (out_23, 1'b1);
  assign out_24 = ~in_1;  // NOT_Gate not_2, 4 bits wide
  nand nand_1 (out_12, in_3, 1'b1);
  nor nor_1 (out_16, in_5, 1'b1);
  buf buffer_1 (buffer_1_out, in_8);
  not not_3 (not_3_out, in_8);
  assign out_26 = in_10 ? ~in_1 : 4'bz;  // Controlled_Inverter controlled_inverter_1
  assign out_14 = ~(in_1 & 4'b1011 & 4'b0011);  // NAND_Gate nand_2, 4 bits wide
  assign out_18 = ~(in_1 | 4'b1001 | 4'b0001);  // NOR_Gate nor_2, 4 bits wide
  xnor xnor_1 (out_20, in_7, 1'b1);
  NotExactlyOne xnor_2[3:0] (.out(out_22), .in0(in_1), .in1(4'b1011), .in2(4'b0011));
  and and_3 (and_3_out, buffer_1_out, not_3_out);
  and and_4 (and_4_out, not_3_out, in_8);
  Counter counter_1 (.clk(and_3_out), .clr(button_1_out));  // open: load, D, count, Q, carry
  Counter counter_2 (.clk(and_4_out), .clr(button_1_out));  // open: load, D, count, Q, carry
  Button button_1 (.out(button_1_out));

  // Other names for the same wires on the sheet: Operator[3:0] = in_1

  // Notes on the sheet:
  //   与门 AND Gate
  //   或门 OR Gate
  //   异或门 XOR Gate
  //   非门 NOT Gate
  //   三态门 Controlled buffer
  //   缓冲器 Buffer
  //   非与门 NAND Gate
  //   非或门 NOR Gate
  //   非异或门 NXOR Gate
  //   1为输入值按位取反，0为高阻态
  //   逆变器 Controlled inverter
  //   对所有输入进行按位操作
  //   缓冲器提供一个短延时，使得上面的与门的输入信号同时改变
endmodule

module \运算与信号处理  (
  input  [7:0] in_1,
  input  [7:0] in_2,
  input  [7:0] in_3,
  input  [15:0] in_4,
  input  [7:0] in_5,
  input  [7:0] in_6,
  input  [7:0] in_7,
  input  [7:0] in_8,
  input  [7:0] in_9,
  input  \进位 ,
  input  \进位_2 ,
  input  \使能信号 ,
  input  \使能信号_2 ,
  input  [1:0] \输出控制 ,
  input  [1:0] \输出控制_2 ,
  input  \使能信号_3 ,
  input  \使能信号_4 ,
  input  [2:0] \输出控制_3 ,
  input  [1:0] \输出控制_4 ,
  output \溢出 ,
  output \借位 
);

  wire bitfinder_1_found, bitselector_1_out, comparator_1_eq, comparator_1_gt, comparator_1_lt,
       comparator_2_eq, comparator_2_gt, comparator_2_lt, priority_encoder_1_gs;
  wire [2:0] bitfinder_1_index, priority_encoder_1_out;
  wire [3:0] decoder_1_out0;
  wire [4:0] bitadder_1_out;
  wire [7:0] adder_1_out, demultiplexer_1_out0, demultiplexer_1_out1, demultiplexer_1_out2,
       demultiplexer_1_out3, divider_1_out, divider_1_rem, multiplexer_1_out, multiplier_1_cout,
       multiplier_1_out, negator_1_out, shifter_1_out, subtractor_1_out;
  wire [15:0] bit_extender_1_out, bit_extender_2_out;

  // Probe on in_1
  // Probe on in_1
  // Probe on in_6
  // Probe on in_6
  Adder adder_1 (.a(in_1), .b(in_6), .out(adder_1_out), .cin(\进位 ), .cout(\溢出 ));
  Subtractor subtractor_1 (.a(in_1), .b(in_6), .out(subtractor_1_out), .bin(\进位_2 ), .bout(\借位 ));
  // Probe on adder_1_out
  // Probe on adder_1_out
  // Probe on subtractor_1_out
  // Probe on subtractor_1_out
  Multiplier multiplier_1 (.a(in_2), .b(in_7), .out(multiplier_1_out), .cin({8{1'b0}}), .cout(multiplier_1_cout));
  Decoder #(.select(2)) decoder_1 (
    .out0(decoder_1_out0[0]), .out1(decoder_1_out0[1]), .out2(decoder_1_out0[2]), .out3(decoder_1_out0[3]),
    .sel(\输出控制_4 ), .en(\使能信号_4 ));
  // Probe on in_2
  // Probe on in_2
  // Probe on in_7
  // Probe on in_7
  // Probe on multiplexer_1_out
  Multiplexer #(.select(2), .width(8)) multiplexer_1 (
    .in0(8'h1), .in1(8'h2), .in2(8'h3), .in3(8'h4), .out(multiplexer_1_out), .sel(\输出控制 ), .en(\使能信号 ));
  // Probe on decoder_1_out0
  // Probe on {multiplier_1_cout, multiplier_1_out}
  // Probe on {multiplier_1_cout, multiplier_1_out}
  // Probe on in_4
  // Probe on in_4
  // Probe on in_8
  // Probe on in_8
  Divider divider_1 (.a(in_4[7:0]), .b(in_8), .out(divider_1_out), .upper(in_4[15:8]), .rem(divider_1_rem));
  // Probe on divider_1_out
  // Probe on divider_1_rem
  Demultiplexer #(.select(2), .width(8)) demultiplexer_1 (
    .out0(demultiplexer_1_out0), .out1(demultiplexer_1_out1), .out2(demultiplexer_1_out2),
    .out3(demultiplexer_1_out3), .in({8{1'b1}}), .sel(\输出控制_2 ), .en(\使能信号_2 ));
  // Probe on 8'h5a
  // Probe on demultiplexer_1_out0
  // Probe on demultiplexer_1_out1
  // Probe on demultiplexer_1_out2
  // Probe on demultiplexer_1_out3
  // Probe on bitselector_1_out
  BitSelector bitselector_1 (.in(8'h5a), .out(bitselector_1_out), .sel(\输出控制_3 ));
  // Probe on negator_1_out
  Negator negator_1 (.in(in_3), .out(negator_1_out));
  // Probe on bit_extender_1_out
  assign bit_extender_1_out = {{8{1'b0}}, in_3};  // Bit_Extender bit_extender_1
  // Probe on bit_extender_2_out
  assign bit_extender_2_out = {{8{in_3[7]}}, in_3};  // Bit_Extender bit_extender_2
  // Probe on bitadder_1_out
  BitAdder bitadder_1 (.in0(in_3), .in1(in_3), .out(bitadder_1_out));
  // Probe on bitfinder_1_index
  BitFinder bitfinder_1 (.in(in_3), .index(bitfinder_1_index), .found(bitfinder_1_found));
  // Probe on bitfinder_1_found
  // Probe on priority_encoder_1_out
  Priority_Encoder #(.disabled(0)) priority_encoder_1 (
    .in0(in_3[0]), .in1(in_3[1]), .in2(in_3[2]), .in3(in_3[3]), .in4(in_3[4]), .in5(in_3[5]), .in6(in_3[6]),
    .in7(in_3[7]), .out(priority_encoder_1_out), .en_in(\使能信号_3 ), .gs(priority_encoder_1_gs));  // open: en_out
  // Probe on priority_encoder_1_gs
  // Probe on in_3
  // Probe on in_3
  // Probe on in_9[2:0]
  // Probe on in_5
  // Probe on in_5
  // Probe on in_9
  // Probe on in_9
  // Probe on comparator_1_gt
  // Probe on comparator_1_eq
  Comparator #(.mode("unsigned")) comparator_1 (
    .a(in_5), .b(in_9), .gt(comparator_1_gt), .eq(comparator_1_eq), .lt(comparator_1_lt));
  // Probe on comparator_1_lt
  // Probe on comparator_2_gt
  // Probe on comparator_2_eq
  Comparator comparator_2 (.a(in_5), .b(in_9), .gt(comparator_2_gt), .eq(comparator_2_eq), .lt(comparator_2_lt));
  // Probe on comparator_2_lt
  Shifter shifter_1 (.in(in_5), .\dist (in_9[2:0]), .out(shifter_1_out));
  // Probe on shifter_1_out

  // Other names for the same wires on the sheet: A1[7:0] = in_1; A2[7:0] = in_2; A3[15:0] = in_4; A4[7:0] = in_3;
  //   A5[7:0] = in_5; B1[7:0] = in_6; B2[7:0] = in_7; B3[7:0] = in_8; B5[7:0] = in_9

  // Notes on the sheet:
  //   加法器Adder / 减法器Subtractor
  //   A+B=
  //   A+B=
  //   A-B=
  //   A-B=
  //   乘法器 Multiplier
  //   多路复用器 Multiplexer
  //   译码器 Decoder
  //   A×B=
  //   A×B=
  //   标0的位置为第0路
  //   输出为控制端口所选的那路输入
  //   使能信号为0，输出0或未知（可设置）
  //   标0的位置为最低位
  //   控制端口所选的比特为1，其余比特为0
  //   使能信号为0，输出0或未知（可设置）
  //   除法器 Divider
  //   选择器 Bit Selector
  //   控制端口所选那路输出为输入的数据
  //   使能信号为0，输出全为0或未知（可设置）
  //   信号分离器 Demultiplexer
  //   输出为控制端口所指的那个比特
  //   标0的位置为第0路
  //   其余路均输出0
  //   优先编码器Priority Encoder
  //   取补器Negator / 拓展器Bit Extender
  //   比特添加器Bit Adder / 比特查找器Bit Finder
  //   取补码
  //   0拓展
  //   符号拓展
  //   计算输入的所有中1的个数
  //   即将所有比特相加
  //   寻找输入中最低位/最高位的0或1
  //   在默认设置中，判断输入是否有1
  //   若有1，给出最低位的1的位置
  //   判断输入是否有1
  //   若有1，给出位数最小的1的位置
  //   比较器Comparator / 移位器Shifter
  //   无符号比较
  //   有符号比较
  //   逻辑左移
endmodule

module \存储器  (
  input  [7:0] in_1,
  input  [7:0] in_2,
  input  \写使能 ,
  input  \时钟信号 ,
  input  \异步置0 ,
  input  \内存使能 ,
  input  \写使能_2 ,
  input  \内存使能_2 ,
  input  \时钟信号_2 ,
  input  \读使能 ,
  input  \异步置0_2 
);

  wire [7:0] ram_1_data, register_1_q, rom_1_data;

  Register register_1 (.D(in_1), .en(\写使能 ), .Q(register_1_q), .clk(\时钟信号 ), .clr(\异步置0 ));
  // Probe on register_1_q
  // Probe on rom_1_data
  ROM rom_1 (.addr(in_2), .data(rom_1_data), .sel(\内存使能 ));
  // Probe on ram_1_data
  RAM #(.bus("separate")) ram_1 (
    .addr(in_2), .din(in_1), .data(ram_1_data), .str(\写使能_2 ), .sel(\内存使能_2 ), .clk(\时钟信号_2 ), .ld(\读使能 ),
    .clr(\异步置0_2 ));

  // Other names for the same wires on the sheet: Addr[7:0] = in_2; Input[7:0] = in_1

  // Notes on the sheet:
  //   写使能为1时，在时钟信号上升沿写入
  //   异步置零为1时，立即将数据置0
  //   contents of rom_1 (hex, n*v repeats v):
  //   0 1 2 3 4 5 6 7 8 9 a b c d e f 10
  //   内存使能为1时，内存可以使用
  //   写使能为1时，在时钟信号上升沿写入
  //   内存使能为1时，内存可以使用
  //   读使能为1时，允许读出
  //   寄存器 Register
  //   RAM（读/写端口分离型）
  //   异步置零为1时，立即将所有位置的数据置0
  //   ROM
endmodule

module \输出模块  (
  input  \时钟信号 ,
  input  \使能 ,
  input  \清空 ,
  input  \使能_2 ,
  input  \清空_2 ,
  input  \左上 ,
  input  \中间 ,
  input  \中上 ,
  input  \右上 ,
  input  \小数点 ,
  input  [3:0] \输入 ,
  input  \左下 ,
  input  \右下 ,
  input  \中下 ,
  input  \小数点_2 
);

  wire button_1_out, keyboard_1_avail, undriven;
  wire [4:0] joystick_1_x, joystick_1_y;
  wire [6:0] keyboard_1_data;

  // Buffer Y has open pins: in=undriven, out=open
  Joystick #(.bits(5)) joystick_1 (.x(joystick_1_x), .y(joystick_1_y));
  // Probe on joystick_1_x
  // Probe on joystick_1_y
  Keyboard keyboard_1 (.clk(\时钟信号 ), .re(\使能 ), .clr(\清空 ), .avail(keyboard_1_avail), .data(keyboard_1_data));
  // Buffer X_2 has open pins: in=undriven, out=open
  // Probe on keyboard_1_avail
  Hex_Digit_Display hex_digit_display_1 (.value(\输入 ), .dp(\小数点_2 ));
  TTY #(.rows(6), .cols(16)) tty_1 (.data(keyboard_1_data), .clk(\时钟信号 ), .we(\使能_2 ), .clr(\清空_2 ));
  _7_Segment_Display u_7_segment_display_1 (
    .g(\中间 ), .f(\左上 ), .a(\中上 ), .b(\右上 ), .e(\左下 ), .d(\中下 ), .c(\右下 ), .dp(\小数点 ));
  Button button_1 (.out(button_1_out));
  DotMatrix #(.dotshape("circle")) dotmatrix_1 (
    .col0(7'b0011100), .col1(7'b0100010), .col2(7'b1001101), .col3(7'b0100010), .col4(7'b0011100));
  LED led_1 (.in(button_1_out));

  // Notes on the sheet:
  //   操纵杆 Joystick
  //   输出端口输出最低位置的字符
  //   每个时钟上升沿，去掉最低位的字符（左侧为位置0）
  //   使能信号为0时，时钟信号无效
  //   清空信号为1时，异步清空缓冲区
  //   使用手型工具点击键盘，随后可以输入字符
  //   输入会存储在缓冲区中
  //   键盘 Keyboard
  //   图中标出了操纵杆的坐标系，左上角为原点(1,1)
  //   使用手型工具可以操作操纵杆
  //   16进制数码管
  //   每个时钟上升沿，从数据端口接受一个ASCII字符并放到显示区末尾
  //   使能信号为0时，时钟信号无效
  //   清空信号为1时，异步清空输出
  //   电传打字机 Teletypewriter
  //   7段(8段)数码管
  //   按钮提供一个短时高电平
  //   使用手型工具点击按钮
  //   按钮Button / LED灯
  //   按列输入，高电平亮
  //   最上面为最低位
  //   LED阵列 LED Matrix
endmodule
