// Logisim project Exp1_RegisterFiles.circ as structural Verilog: 3 circuits, main circuit RegisterFiles
module RegisterFiles (
  input  in_1,
  input  [4:0] in_2,
  input  [4:0] in_3,
  input  [4:0] in_4,
  input  in_5,
  input  [31:0] in_6,
  output [31:0] out_7,
  output [31:0] out_8
);

  Register #(.width(32)) register_1 (.D(in_6), .clk(in_1));  // open: en, Q, clr
  Register #(.width(32)) register_2 (.D(in_6), .clk(in_1));  // open: en, Q, clr
  Register #(.width(32)) register_3 (.D(in_6), .clk(in_1));  // open: en, Q, clr
  Register #(.width(32)) register_4 (.D(in_6), .clk(in_1));  // open: en, Q, clr
  Multiplexer #(.select(2), .width(32)) multiplexer_1 (.out(out_7), .sel(in_2[1:0]));  // open: in0, in1, in2, in3, en
  Multiplexer #(.select(2), .width(32)) multiplexer_2 (.out(out_8), .sel(in_3[1:0]));  // open: in0, in1, in2, in3, en
  Demultiplexer #(.select(2)) demultiplexer_1 (.in(in_5), .sel(in_4[1:0]));  // open: out0, out1, out2, out3, en

  // Other names for the same wires on the sheet: A1[4:0] = in_2; A2[4:0] = in_3; A3[4:0] = in_4; CLK = in_1;
  //   RD1[31:0] = out_7; RD2[31:0] = out_8; WD[31:0] = in_6; WE = in_5

  // Notes on the sheet:
  //   输入端口
  //   输出端口
endmodule

module AutoTest (
  input  in_1
);

  wire and_1_out, CLK, comparator_1_lt, comparator_2_gt, Continue, E, END, not_1_out, not_2_out, or_1_out,
       PASS, RST, Succ, testmemory_1_out_11;
  wire [4:0] A1, A2, A3;
  wire [7:0] CNT, counter_2_q, Line;
  wire [31:0] C1, C2, D, R1, R2;

  Button button_1 (.out(RST));
  Clock clock_1 (.out(CLK));
  not not_1 (not_1_out, in_1);
  Counter counter_1 (.count(Continue), .Q(CNT), .clk(CLK), .clr(RST));  // open: load, D, carry
  Comparator comparator_1 (.a(CNT), .b(8'ha), .lt(comparator_1_lt));  // open: gt, eq
  and and_1 (and_1_out, comparator_1_lt, Succ);
  Counter counter_2 (.count(and_1_out), .Q(counter_2_q), .clk(CLK), .clr(RST));  // open: load, D, carry
  or or_1 (or_1_out, not_1_out, Succ);
  not not_2 (not_2_out, END);
  LED led_1 (.in(PASS));
  LED led_2 (.in(END));
  not not_3 (END, comparator_2_gt);
  Comparator comparator_2 (.a(8'ha), .b(CNT), .gt(comparator_2_gt));  // open: eq, lt
  Adder adder_1 (.a(CNT), .b(8'h3), .out(Line));  // open: cin, cout
  RegisterFiles registerfiles_1 (
    .in_5(E), .in_3(A2), .in_1(testmemory_1_out_11), .in_4(A3), .out_7(R1), .in_6(D), .out_8(R2), .in_2(A1));
  Comparator comparator_3 (.a(counter_2_q), .b(8'ha), .eq(PASS));  // open: gt, lt
  and and_2 (Continue, or_1_out, not_2_out);
  TestMemory testmemory_1 (
    .in_1(CNT), .in_3(R1), .in_4(R2), .in_2(CLK), .out_7(D), .out_8(A1), .out_9(A2), .out_10(A3),
    .out_11(testmemory_1_out_11), .out_12(E), .out_13(Succ), .out_5(C1), .out_6(C2));
  // Probe on Line
  // Probe on A1
  // Probe on A2
  // Probe on A3
  // Probe on R1
  // Probe on R2
  // Probe on D
  // Probe on C1
  // Probe on C2
  LED led_3 (.in(E));

  // Other names for the same wires on the sheet: Debug = in_1

  // Notes on the sheet:
  //   信号端口
  //   评测电路
  //   评测信号
  //   PASS
  //   Finished
  //   读地址/数据1
  //   读地址/数据2
  //   写地址/数据/使能
  //   调试信号
  //   行号
  //   正确数据1
  //   正确数据2
endmodule

module TestMemory (
  input  [7:0] in_1,
  input  in_2,
  input  [31:0] in_3,
  input  [31:0] in_4,
  output [31:0] out_5,
  output [31:0] out_6,
  output [31:0] out_7,
  output [4:0] out_8,
  output [4:0] out_9,
  output [4:0] out_10,
  output out_11,
  output out_12,
  output out_13
);

  wire comparator_1_eq, comparator_2_eq;

  ROM #(.dataWidth(7)) rom_1 (.addr(in_1), .data({out_8[1:0], out_9[1:0], out_10[1:0], out_12}));  // open: sel
  ROM #(.dataWidth(32)) rom_2 (.addr(in_1), .data(out_7));  // open: sel
  ROM #(.dataWidth(32)) rom_3 (.addr(in_1), .data(out_5));  // open: sel
  ROM #(.dataWidth(32)) rom_4 (.addr(in_1), .data(out_6));  // open: sel
  Comparator #(.width(32)) comparator_1 (.a(in_3), .b(out_5), .eq(comparator_1_eq));  // open: gt, lt
  Comparator #(.width(32)) comparator_2 (.a(in_4), .b(out_6), .eq(comparator_2_eq));  // open: gt, lt
  Pull_Resistor pull_resistor_1 (.node(comparator_1_eq));
  and and_1 (out_13, comparator_1_eq, comparator_2_eq);
  Pull_Resistor pull_resistor_2 (.node(comparator_2_eq));

  assign out_8[4:2] = 3'b000;
  assign out_9[4:2] = 3'b000;
  assign out_10[4:2] = 3'b000;
  assign out_11 = in_2;

  // Other names for the same wires on the sheet: WE = out_12; A1[1:0] = out_8[1:0]; A2[1:0] = out_9[1:0];
  //   A3[1:0] = out_10[1:0]; CLK = in_2; CNT[7:0] = in_1; Correct1[31:0] = out_5; Correct2[31:0] = out_6;
  //   RD1[31:0] = in_3; RD2[31:0] = in_4; succ = out_13; WD[31:0] = out_7

  // Notes on the sheet:
  //   输入端口
  //   A1/A2/A3/WE
  //   WD
  //   RD1
  //   RD2
  //   contents of rom_1 (hex, n*v repeats v):
  //   0 1 1 3 d 37 5b 6a 4c 10
  //   contents of rom_2 (hex, n*v repeats v):
  //   0 ffffffff ffff0000 1100f 2200f 3300f 44ff0 fffffff0 101ffff
  //   contents of rom_3 (hex, n*v repeats v):
  //   5*0 1100f 2200f 3300f 2200f
  //   contents of rom_4 (hex, n*v repeats v):
  //   4*0 1100f 2200f 3300f 44ff0 44ff0 2200f
  //   输出端口
endmodule
